# Fritzing sketch schematic_v2 (saved by Fritzing 0.9.0b)
breadboards: 1

parts:
  RHT03 = Humidity and Temperature Sensor RHT03
  BMP085 = Barometric Pressure Sensor - BMP085 Breakout
  Rain_Gauge_RJ11_Pins_1_2_5_6_not_used = RJ11 Jack [package=rj11-6]
  J2 = Basic Servo
  Εξάρτημα2 = Arduino Mega 2560 (Rev3)
  R1 = Resistor [package="2010 [SMD]"]
  R2 = Resistor [package="2010 [SMD]"]
  Vane_&_Anemomete_Pins_1_6_not_used = RJ11 Jack [package=rj11-6]
  R3 = Resistor [package="2010 [SMD]"]
  R4 = Resistor [package="2010 [SMD]"]
  J3 = Basic Servo
  C1 = Electrolytic Capacitor [capacitance=1µF package="100 mil [THT, electrolytic]"]
  C2 = Electrolytic Capacitor [capacitance=1µF package="100 mil [THT, electrolytic]"]

nets:
  VCC: RHT03.Vcc, J2.vcc, Εξάρτημα2.5V, R2.Pin_0, Vane_&_Anemomete_Pins_1_6_not_used.2, Vane_&_Anemomete_Pins_1_6_not_used.3, R4.Pin_0, J3.vcc, C1.+, C2.-
  N1: RHT03.Data-signal, Εξάρτημα2.D9_PWM, R1.Pin_1
  GND: RHT03.GND_2, BMP085.GND, Rain_Gauge_RJ11_Pins_1_2_5_6_not_used.4, J2.gnd, Εξάρτημα2.GND, J3.gnd, C1.-, C2.+
  VCC_2: BMP085.VCC, Εξάρτημα2.3V3
  N2: BMP085.SDA, Εξάρτημα2.D20/SDA
  N3: Rain_Gauge_RJ11_Pins_1_2_5_6_not_used.3, Εξάρτημα2.D3_PWM, R2.Pin_1
  N4: J2.pulse, Εξάρτημα2.D40
  N5: Εξάρτημα2.A5, Vane_&_Anemomete_Pins_1_6_not_used.5, R4.Pin_1
  N6: Εξάρτημα2.D2_PWM, R3.Pin_1
  N7: Εξάρτημα2.D39, J3.pulse
  N8: Vane_&_Anemomete_Pins_1_6_not_used.4, R3.Pin_0
